// Logisim project bcd.circ as structural Verilog: 1 circuit, main circuit main
module main (
);

  wire a, and_1_out, and_2_out, and_3_out, and_4_out, and_5_out, and_6_out, and_7_out, and_8_out, and_9_out,
       and_10_out, and_11_out, and_12_out, and_13_out, and_14_out, and_15_out, and_16_out, and_17_out,
       and_18_out, and_19_out, and_20_out, and_21_out, and_22_out, and_23_out, and_24_out, and_25_out,
       and_26_out, and_27_out, and_28_out, b, c, clock_1_out, d, e, f, g, not_1_out, not_3_out, not_6_out,
       not_7_out, not_10_out, not_11_out, not_12_out, not_13_out, not_14_out, not_15_out, not_16_out,
       not_17_out, not_18_out, not_19_out, not_20_out, not_22_out, not_23_out, not_24_out, not_26_out,
       not_27_out, not_28_out, Reset_out, stop, w0, w1, w2, w3;

  _7_Segment_Display u_7_segment_display_1 (.g(g), .f(f), .a(a), .b(b), .e(e), .d(d), .c(c));  // open: dp
  Clock clock_1 (.out(clock_1_out));
  not not_1 (not_1_out, stop);
  // Probe on {w3, w2, w1, w0}
  and and_1 (and_1_out, clock_1_out, not_1_out);
  // NOT_Gate not_2 has open pins: in=w0, out=open
  not not_3 (not_3_out, w1);
  // NOT_Gate not_4 has open pins: in=w2, out=open
  // NOT_Gate not_5 has open pins: in=w3, out=open
  not not_6 (not_6_out, w0);
  not not_7 (not_7_out, w1);
  // NOT_Gate not_8 has open pins: in=w2, out=open
  // NOT_Gate not_9 has open pins: in=w3, out=open
  TTY #(.rows(10), .cols(1)) tty_1 (.data({3'b100, d, c, b, a}), .clk(and_1_out), .clr(Reset_out));  // open: we
  Counter #(.width(4), .max('h9), .ongoal("stay")) counter_1 (
    .Q({w3, w2, w1, w0}), .carry(stop), .clk(and_1_out), .clr(Reset_out));  // open: load, D, count
  buf and_2 (and_2_out, w0);  // AND_Gate
  buf and_3 (and_3_out, not_3_out);  // AND_Gate
  buf and_4 (and_4_out, w2);  // AND_Gate
  buf and_5 (and_5_out, w3);  // AND_Gate
  TTY #(.rows(10), .cols(1)) tty_2 (.data({4'b0110, g, f, e}), .clk(and_1_out), .clr(Reset_out));  // open: we
  buf and_6 (and_6_out, w3);  // AND_Gate
  and and_7 (and_7_out, not_7_out, not_6_out);
  and and_8 (and_8_out, w2, not_7_out);
  and and_9 (and_9_out, w2, w1, not_6_out);
  Button Reset (.out(Reset_out));
  or or_1 (c, and_2_out, and_3_out, and_4_out, and_5_out);
  or or_2 (f, and_6_out, and_7_out, and_8_out, and_9_out);
  not not_10 (not_10_out, w0);
  not not_11 (not_11_out, w1);
  not not_12 (not_12_out, w2);
  not not_13 (not_13_out, w3);
  not not_14 (not_14_out, w0);
  not not_15 (not_15_out, w1);
  not not_16 (not_16_out, w2);
  not not_17 (not_17_out, w3);
  not not_18 (not_18_out, w0);
  not not_19 (not_19_out, w1);
  not not_20 (not_20_out, w2);
  // NOT_Gate not_21 has open pins: in=w3, out=open
  buf and_10 (and_10_out, w3);  // AND_Gate
  and and_11 (and_11_out, not_10_out, not_11_out, not_12_out);
  buf and_12 (and_12_out, w1);  // AND_Gate
  and and_13 (and_13_out, not_13_out, w2, w0);
  and and_14 (and_14_out, not_14_out, w1);
  and and_15 (and_15_out, w1, not_16_out, not_17_out);
  and and_16 (and_16_out, w2, not_15_out, w0);
  and and_17 (and_17_out, not_16_out, not_15_out, not_14_out);
  buf and_18 (and_18_out, w3);  // AND_Gate
  buf and_19 (and_19_out, w3);  // AND_Gate
  and and_20 (and_20_out, w1, not_18_out);
  and and_21 (and_21_out, w2, not_19_out);
  and and_22 (and_22_out, not_20_out, w1, w0);
  or or_3 (a, and_10_out, and_11_out, and_12_out, and_13_out);
  or or_4 (d, and_14_out, and_15_out, and_16_out, and_17_out, and_18_out);
  or or_5 (g, and_19_out, and_20_out, and_21_out, and_22_out);
  not not_22 (not_22_out, w0);
  not not_23 (not_23_out, w1);
  not not_24 (not_24_out, w2);
  // NOT_Gate not_25 has open pins: in=w3, out=open
  not not_26 (not_26_out, w0);
  not not_27 (not_27_out, w1);
  not not_28 (not_28_out, w2);
  // NOT_Gate not_29 has open pins: in=w3, out=open
  buf and_23 (and_23_out, w3);  // AND_Gate
  buf and_24 (and_24_out, not_24_out);  // AND_Gate
  and and_25 (and_25_out, not_22_out, not_23_out);
  and and_26 (and_26_out, w1, w0);
  and and_27 (and_27_out, w1, not_26_out);
  and and_28 (and_28_out, not_27_out, not_26_out, not_28_out);
  or or_6 (b, and_23_out, and_24_out, and_25_out, and_26_out);
  or or_7 (e, and_27_out, and_28_out);

  // Notes on the sheet:
  //   C
  //   F
  //   O
  //   F
  //   K
  //   O
  //   F
  //   M
  //   M
  //   G
  //   O
  //   3
  //   0
  //   5
  //   4
  //   6
  //   6
  //   7
  //   0
  //   7
  //   A
  //   D
  //   G
  //   B
  //   E
endmodule
