// Logisim project 6test.circ as structural Verilog: 1 circuit, main circuit main
module main (
);

  wire _4_Counter_carry, A_q, A_qn, and_1_out, and_2_out, and_3_out, and_4_out, and_5_out, B_q, B_qn, C_q,
       C_qn, CLK, clock_1_out, go, not_1_out, or_1_out, or_2_out, or_3_out, Q, Reset_out, w, xor_1_out;
  wire [1:0] _4_Counter_q;
  wire [4:0] _32_Counter_q;

  not not_1 (not_1_out, w);
  xor xor_1 (xor_1_out, B_q, w);
  and and_1 (and_1_out, A_qn, B_q, C_qn);
  and and_2 (and_2_out, A_q, B_qn, C_qn);
  and and_3 (and_3_out, A_qn, C_qn, not_1_out);
  or or_1 (or_1_out, A_q, xor_1_out);
  TTY #(.rows(17), .cols(4)) tty_1 (.data({6'b011000, Q}), .clk(CLK), .we(go), .clr(Reset_out));
  and and_4 (and_4_out, C_qn, or_1_out);
  or or_2 (or_2_out, A_q, C_q, w);
  Button Reset (.out(Reset_out));
  or or_3 (or_3_out, and_1_out, and_2_out, and_3_out);
  and and_5 (and_5_out, B_q, or_2_out);
  and and_6 (CLK, clock_1_out, go);
  Clock clock_1 (.out(clock_1_out));
  // Probe on _4_Counter_q
  Counter #(.width(2), .max('h3)) _4_Counter (
    .Q(_4_Counter_q), .carry(_4_Counter_carry), .clk(CLK), .clr(Reset_out));  // open: load, D, count
  D_Flip_Flop A (.clk(CLK), .D(and_4_out), .Q(A_q), .Qn(A_qn));  // open: preset, en, reset
  D_Flip_Flop B (.clk(CLK), .D(or_3_out), .Q(B_q), .Qn(B_qn));  // open: preset, en, reset
  D_Flip_Flop C (.clk(CLK), .D(and_5_out), .Q(C_q), .Qn(C_qn));  // open: preset, en, reset
  // Probe on _32_Counter_q[3:0]
  Counter #(.width(5), .max('h1f), .trigger("falling")) _32_Counter (
    .Q(_32_Counter_q), .clk(_4_Counter_carry), .clr(Reset_out));  // open: load, D, count, carry
  // Probe on w
  BitSelector #(.width(4)) bitselector_1 (.in(_32_Counter_q[3:0]), .out(w), .sel(_4_Counter_q));
  not not_2 (go, _32_Counter_q[4]);
  and and_7 (Q, w, A_qn, B_qn, C_q);

  // Notes on the sheet:
  //   11 gates
  //   0000
  //   1000
  //   0100
  //   1100
  //   0010
  //   1010
  //   0110
  //   1110
  //   0001
  //   1001
  //   0101
  //   1101
  //   0011
  //   1011
  //   0111
  //   1111
  //   1
  //   1
endmodule
