// Logisim project alu.circ as structural Verilog: 1 circuit, main circuit main
module main (
);

  wire A0, A1, A2, Ad0, Ad1, Ad2, Ad3, and_1_out, B0, B1, B2, C0, C1, c1_out, C2, c2_out, CIN, clock_1_out,
       g0p1_out, g_1p0_out, g_1p0p1_out, not_2_out, Reset_out, S0, S1, stop;
  wire [2:0] g0_out, not_1_out, p0_out, s0_out;
  wire [11:3] rom_1_data;

  not not_1 (not_1_out[0], A0);
  and g0 (g0_out[0], A0, B0);
  or p0 (p0_out[0], B0, A0);
  xor u_s0 (s0_out[0], B0, A0, CIN);
  and g_1p0 (g_1p0_out, CIN, p0_out[0]);
  or u_c1 (c1_out, g_1p0_out, g0_out[0]);
  Clock clock_1 (.out(clock_1_out));
  not not_2 (not_2_out, stop);
  not not_3 (not_1_out[1], A1);
  // Probe on {C2, C1, C0}
  and and_1 (and_1_out, clock_1_out, not_2_out);
  and g1 (g0_out[1], A1, B1);
  or p1 (p0_out[1], B1, A1);
  xor u_s1 (s0_out[1], B1, A1, c1_out);
  and g_1p0p1 (g_1p0p1_out, CIN, p0_out[0], p0_out[1]);
  // Probe on CIN
  // Probe on {S1, S0}
  TTY #(.rows(1), .cols(10)) tty_1 (.data({4'b0110, C2, C1, C0}), .clk(and_1_out), .clr(Reset_out));  // open: we
  Counter #(.width(4), .max('ha), .ongoal("stay")) counter_1 (
    .Q({Ad3, Ad2, Ad1, Ad0}), .carry(stop), .clk(and_1_out), .clr(Reset_out));  // open: load, D, count
  ROM #(.addrWidth(4), .dataWidth(12)) rom_1 (
    .addr({Ad3, Ad2, Ad1, Ad0}),
    .data({rom_1_data[11], CIN, S1, S0, rom_1_data[7], B2, B1, B0, rom_1_data[3], A2, A1, A0}));  // open: sel
  and g0p1 (g0p1_out, g0_out[0], p0_out[1]);
  or u_c2 (c2_out, g_1p0p1_out, g0p1_out, g0_out[1]);
  // Probe on {B2, B1, B0}
  // Probe on {rom_1_data[11], CIN, S1, S0, rom_1_data[7], B2, B1, B0, rom_1_data[3], A2, A1, A0}
  // Probe on {A2, A1, A0}
  Button Reset (.out(Reset_out));
  and g2 (g0_out[2], A2, B2);
  not not_4 (not_1_out[2], A2);
  or p2 (p0_out[2], B2, A2);
  xor s2 (s0_out[2], B2, A2, c2_out);
  Multiplexer #(.select(2), .width(3)) multiplexer_1 (
    .in0(g0_out), .in1(p0_out), .in2(not_1_out), .in3(s0_out), .out({C2, C1, C0}), .sel({S1, S0}));  // open: en

  // Notes on the sheet:
  //   adds 48 to make printable
  //   contents of rom_1 (hex, n*v repeats v):
  //   53 62 153 162 205 202 377 353 764 723
  //   5 & 3, 6 & 2, 5 | 3, 6 | 2, ~5, ~2, 7 + 7 + 0, 5 + 3 + 0, 6 + 4 + 1, 3 + 2 + 1
  //   1276256036
  //   NOT
  //   ADD/SUB
  //   AND
  //   OR
endmodule
