// Logisim project 4.circ as structural Verilog: 1 circuit, main circuit main
module main (
);

  wire and_1_out, and_2_out, and_3_out, and_5_out, and_6_out, and_7_out, and_8_out, and_9_out, and_10_out,
       and_11_out, and_12_out, Carry, CLK, clock_1_out, counter_1_carry, D0, D1, D2, D3, Enable, Load,
       multiplexer_1_out, multiplexer_2_out, multiplexer_3_out, multiplexer_4_out, not_1_out, not_2_out,
       not_3_out, not_4_out, not_5_out, not_6_out, not_7_out, not_8_out, not_9_out, or_1_out, or_2_out,
       or_3_out, or_4_out, Q0, Q1, Q2, Q3;
  wire [5:1] counter_1_q;

  and and_1 (and_1_out, Enable, Q0);
  and and_2 (and_2_out, and_1_out, Q1);
  and and_3 (and_3_out, and_2_out, Q2);
  and and_4 (Carry, and_3_out, Q3);
  not not_1 (not_1_out, Q0);
  not not_2 (not_2_out, D0);
  not not_3 (not_3_out, Q1);
  not not_4 (not_4_out, D1);
  not not_5 (not_5_out, Q2);
  not not_6 (not_6_out, D2);
  not not_7 (not_7_out, Q3);
  not not_8 (not_8_out, D3);
  and and_5 (and_5_out, not_1_out, D0);
  and and_6 (and_6_out, Q0, not_2_out);
  and and_7 (and_7_out, not_3_out, D1);
  and and_8 (and_8_out, Q1, not_4_out);
  and and_9 (and_9_out, not_5_out, D2);
  and and_10 (and_10_out, Q2, not_6_out);
  and and_11 (and_11_out, not_7_out, D3);
  and and_12 (and_12_out, Q3, not_8_out);
  or or_1 (or_1_out, and_5_out, and_6_out);
  or or_2 (or_2_out, and_7_out, and_8_out);
  or or_3 (or_3_out, and_9_out, and_10_out);
  or or_4 (or_4_out, and_11_out, and_12_out);
  Multiplexer multiplexer_1 (.in0(Enable), .in1(or_1_out), .out(multiplexer_1_out), .sel(Load));  // open: en
  Multiplexer multiplexer_2 (.in0(and_1_out), .in1(or_2_out), .out(multiplexer_2_out), .sel(Load));  // open: en
  Multiplexer multiplexer_3 (.in0(and_2_out), .in1(or_3_out), .out(multiplexer_3_out), .sel(Load));  // open: en
  Multiplexer multiplexer_4 (.in0(and_3_out), .in1(or_4_out), .out(multiplexer_4_out), .sel(Load));  // open: en
  T_Flip_Flop t_ff_1 (.clk(CLK), .T(multiplexer_1_out), .Q(Q0));  // open: Qn, preset, reset, en
  T_Flip_Flop t_ff_2 (.clk(CLK), .T(multiplexer_2_out), .Q(Q1));  // open: Qn, preset, reset, en
  T_Flip_Flop t_ff_3 (.clk(CLK), .T(multiplexer_3_out), .Q(Q2));  // open: Qn, preset, reset, en
  T_Flip_Flop t_ff_4 (.clk(CLK), .T(multiplexer_4_out), .Q(Q3));  // open: Qn, preset, reset, en
  Counter #(.width(6), .max('h24)) counter_1 (
    .Q({counter_1_q[5], Load, D3, counter_1_q[2:1], D0}), .carry(counter_1_carry), .clk(CLK));  // open: load, D, count, clr
  and and_13 (CLK, clock_1_out, not_9_out);
  not not_9 (not_9_out, counter_1_carry);
  Clock clock_1 (.out(clock_1_out));
  TTY #(.rows(1), .cols(37)) tty_1 (.data({2'b10, Carry, Q3, Q2, Q1, Q0}), .clk(CLK));  // open: we, clr
  not not_10 (Enable, counter_1_q[5]);
  or or_5 (D1, Enable, counter_1_q[1]);
  or or_6 (D2, counter_1_q[2], Load);

  // Notes on the sheet:
  //   @ABCDEFGHIJKLMN_@FGFGFGFGN_N_N_N0000
endmodule
