// Logisim project 8test.circ as structural Verilog: 1 circuit, main circuit main
module main (
);

  wire _4_Counter_carry, A_qn, and_2_out, and_3_out, and_4_out, and_5_out, and_6_out, and_7_out, and_8_out,
       and_9_out, and_10_out, and_11_out, and_12_out, and_13_out, and_14_out, and_15_out, and_17_out,
       and_18_out, and_19_out, B_qn, C_qn, CLK, clock_1_out, go, I5, I10, I25, not_1_out, not_2_out, O5, O10,
       OM, or_3_out, or_4_out, or_5_out, Reset_out;
  wire [1:1] and_16_out;
  wire [2:0] C_q;
  wire [4:0] _4_Counter_q;

  TTY #(.rows(1), .cols(33)) tty_1 (.data({4'b1000, OM, O10, O5}), .clk(CLK), .we(go), .clr(Reset_out));
  not not_1 (not_1_out, I5);
  Button Reset (.out(Reset_out));
  and and_1 (CLK, clock_1_out, go);
  Clock clock_1 (.out(clock_1_out));
  // Probe on _4_Counter_q
  Counter #(.width(5), .max('h1f)) _4_Counter (
    .Q(_4_Counter_q), .carry(_4_Counter_carry), .clk(CLK), .clr(Reset_out));  // open: load, D, count
  not not_2 (not_2_out, I25);
  not not_3 (go, _4_Counter_carry);
  and and_2 (and_2_out, I25, C_q[0]);
  and and_3 (and_3_out, not_2_out, 1'b0);
  // Probe on I5
  ROM #(.addrWidth(5), .dataWidth(3)) rom_1 (.addr(_4_Counter_q), .data({I25, I10, I5}));  // open: sel
  or or_1 (O10, and_2_out, and_3_out);
  and and_4 (and_4_out, I25, C_q[1]);
  and and_5 (and_5_out, not_2_out, and_16_out[1]);
  // Probe on I10
  // Probe on I25
  or or_2 (O5, and_4_out, and_5_out);
  and and_6 (and_6_out, C_q[1], C_qn, I10);
  and and_7 (and_7_out, B_qn, I5);
  and and_8 (and_8_out, C_q[0], I5, A_qn);
  and and_9 (and_9_out, C_q[0], I10, B_qn, A_qn);
  and and_10 (and_10_out, I10, B_qn, A_qn);
  and and_11 (and_11_out, C_q[0], I5, A_qn);
  and and_12 (and_12_out, C_q[1], I5, A_qn);
  and and_13 (and_13_out, C_q[1], not_1_out, I10, C_qn);
  and and_14 (and_14_out, I10, C_q[0], B_qn, A_qn);
  and and_15 (and_15_out, I5, C_q[1], C_q[0], A_qn);
  or or_3 (or_3_out, and_14_out, and_15_out);
  or or_4 (or_4_out, and_6_out, and_7_out, and_8_out, and_9_out);
  or or_5 (or_5_out, and_10_out, and_11_out, and_12_out, and_13_out);
  D_Flip_Flop A (.clk(CLK), .D(or_3_out), .Q(C_q[2]), .Qn(A_qn));  // open: preset, en, reset
  D_Flip_Flop B (.clk(CLK), .D(or_4_out), .Q(C_q[1]), .Qn(B_qn));  // open: preset, en, reset
  D_Flip_Flop C (.clk(CLK), .D(or_5_out), .Q(C_q[0]), .Qn(C_qn));  // open: preset, en, reset
  and and_16 (and_16_out[1], C_q[2], I10);
  and and_17 (and_17_out, C_q[2], C_q[0], I10);
  and and_18 (and_18_out, C_q[2], C_q[0], I5);
  and and_19 (and_19_out, A_qn, C_q[1], C_q[0], I10);
  or or_6 (OM, and_19_out, and_18_out, and_17_out, I25);

  // Notes on the sheet:
  //   24 Gates
  //   D@@@@D@@@D@@E@E@F@@G@@G@F@@E@@@
  //   contents of rom_1 (hex, n*v repeats v):
  //   4 6*1 2 1 1 2 2 2 1 4 2 4 2 2 4 1 2 4 2 4 2 2 2 1 1 1 2
endmodule
