// Logisim project cpu.circ as structural Verilog: 9 circuits, main circuit main
module main (
  output [8:0] out_1,
  output [8:0] out_2,
  output [21:0] instruction,
  output [2:0] out_4,
  output [8:0] out_5,
  output [8:0] out_6,
  output [8:0] out_7,
  output [8:0] out_8,
  output [8:0] out_9,
  output [8:0] out_10,
  output [8:0] out_11,
  output [8:0] out_12,
  output [3:0] out_13
);

  wire clock_1_out, comparator_1_lt, counter_1_carry, decoder_1_out8, decoder_1_out9, decoder_1_out10,
       decoder_1_out11, decoder_1_out15, Immediate, not_1_out, not_2_out, Reset, TClock, Write_Enable;
  wire [2:0] multiplexer_5_out, rom_1_data;
  wire [3:0] multiplexer_6_out;
  wire [4:0] counter_1_q, MSB;
  wire [6:0] adder_1_out, LSB;

  Decoder #(.select(4)) decoder_1 (
    .out8(decoder_1_out8), .out9(decoder_1_out9), .out10(decoder_1_out10), .out11(decoder_1_out11),
    .out15(decoder_1_out15), .sel(instruction[21:18]));  // open: out0, out1, out2, out3, out4, out5, out6, out7, out12, out13, out14, en
  Counter_RAM Counter_RAM (.counter_clock(TClock), .HALT(decoder_1_out15), .instruction(instruction));
  not not_1 (not_1_out, TClock);
  Multiplexer multiplexer_1 (.in0(not_1_out), .in1(1'b0), .out(Write_Enable), .sel(decoder_1_out11));  // open: en
  Multiplexer #(.width(3)) multiplexer_2 (
    .in0(instruction[11:9]), .in1(3'b111), .out(out_4), .sel(decoder_1_out11));  // open: en
  or or_1 (Immediate, decoder_1_out8, decoder_1_out9, decoder_1_out10);
  Multiplexer #(.select(3), .width(9)) multiplexer_3 (
    .in0(out_5), .in1(out_7), .in2(out_9), .in3(out_11), .in4(out_6), .in5(out_8), .in6(out_10), .out(out_2),
    .sel(instruction[17:15]));  // open: in7, en
  TTY #(.rows(33), .cols(1)) tty_1 (.data({2'b10, MSB}), .clk(TClock), .clr(Reset));  // open: we
  Multiplexer #(.select(3), .width(9)) multiplexer_4 (
    .in0(out_5), .in1(out_7), .in2(out_9), .in3(out_11), .in4(out_6), .in5(out_8), .in6(out_10),
    .in7(instruction[8:0]), .out(out_1), .sel(multiplexer_5_out));  // open: en
  TTY #(.rows(33), .cols(1)) tty_2 (.data(LSB), .clk(TClock), .clr(Reset));  // open: we
  Multiplexer #(.width(3)) multiplexer_5 (
    .in0(instruction[14:12]), .in1(3'b111), .out(multiplexer_5_out), .sel(Immediate));  // open: en
  ALU ALU (.A_Input(out_2), .B_Input(out_1), .Operation(instruction[21:18]), .Alu_output(out_12));
  Button u_Reset (.out(Reset));
  Counter #(.width(5), .max('h1f), .ongoal("stay")) counter_1 (
    .Q(counter_1_q), .carry(counter_1_carry), .clk(TClock), .clr(Reset));  // open: load, D, count
  Multiplexer #(.select(3), .width(9), .disabled(0), .enable("false")) multiplexer_6 (
    .in0(out_5), .in1(out_7), .in2(out_9), .in3(out_11), .in4(out_6), .in5(out_8), .in6(out_10),
    .out({MSB, multiplexer_6_out}), .sel(rom_1_data));  // open: in7
  not not_2 (not_2_out, counter_1_carry);
  Clock clock_1 (.out(clock_1_out));
  and and_1 (TClock, not_2_out, clock_1_out);
  ROM #(.addrWidth(5), .dataWidth(3)) rom_1 (.addr(counter_1_q), .data(rom_1_data));  // open: sel
  // Probe on {3'b011, multiplexer_6_out}
  // Probe on {2'b10, MSB}
  Comparator #(.width(7)) comparator_1 (
    .a(7'b0111001), .b({3'b011, multiplexer_6_out}), .lt(comparator_1_lt));  // open: gt, eq
  // Probe on LSB
  Multiplexer #(.width(7), .disabled(0), .enable("false")) multiplexer_7 (
    .in0({3'b011, multiplexer_6_out}), .in1(adder_1_out), .out(LSB), .sel(comparator_1_lt));
  Adder #(.width(7)) adder_1 (.a({3'b011, multiplexer_6_out}), .b(7'b0000111), .out(adder_1_out));  // open: cin, cout
  Register_Bank Register_Bank (
    .Write_Enable(Write_Enable), .Destination_Register(out_4), .bank_clock(TClock), .Writing_(out_12),
    .Register_0(out_5), .Register_1(out_7), .Register_2(out_9), .Register_3(out_11), .Register_4(out_6),
    .Register_5(out_8), .Register_6(out_10));

  assign out_13 = instruction[21:18];

  // Other names for the same wires on the sheet: DATA[8:0] = instruction[8:0]; Destination_Register[2:0] = out_4;
  //   MUX_A[2:0] = instruction[17:15]; MUX_B[2:0] = instruction[14:12]; OPCODE[3:0] = instruction[21:18];
  //   R0[8:0] = out_5; R1[8:0] = out_7; R2[8:0] = out_9; R3[8:0] = out_11; R4[8:0] = out_6; R5[8:0] = out_8;
  //   R6[8:0] = out_10; Writing[8:0] = out_12

  // Notes on the sheet:
  //   MUXA
  //   @0
  //   JA
  //   E5
  //   @0
  //   OF
  //   U5
  //   OF
  //   E5
  //   E5
  //   U4
  //   E5
  //   E5
  //   U4
  //   _F
  //   _F
  //   _F
  //   AF
  //   AF
  //   AF
  //   @0
  //   AE
  //   AE
  //   AE
  //   _E
  //   OF
  //   ^0
  //   J9
  //   P1
  //   R0
  //   R0
  //   _F
  //   MUXB
  //   contents of rom_1 (hex, n*v repeats v):
  //   0 0 1 2 3 4 5 6 6 2 3 4 5 6 6 0 1 2 3 4 5 6 6 2 3 4 5 6 6 6
endmodule

module Register_Bank (
  input  Write_Enable,
  input  [2:0] Destination_Register,
  input  bank_clock,
  input  [8:0] Writing_,
  output [8:0] Register_0,
  output [8:0] Register_1,
  output [8:0] Register_2,
  output [8:0] Register_3,
  output [8:0] Register_4,
  output [8:0] Register_5,
  output [8:0] Register_6
);

  wire and_1_out, and_2_out, and_3_out, and_4_out, and_5_out, and_6_out, and_7_out, decoder_1_out0,
       decoder_1_out1, decoder_1_out2, decoder_1_out3, decoder_1_out4, decoder_1_out5, decoder_1_out6;
  wire [8:0] multiplexer_1_out, multiplexer_2_out, multiplexer_3_out, multiplexer_4_out, multiplexer_5_out,
       multiplexer_6_out, multiplexer_7_out;

  Decoder #(.select(3)) decoder_1 (
    .out0(decoder_1_out0), .out1(decoder_1_out1), .out2(decoder_1_out2), .out3(decoder_1_out3),
    .out4(decoder_1_out4), .out5(decoder_1_out5), .out6(decoder_1_out6), .sel(Destination_Register));  // open: out7, en
  and and_1 (and_1_out, decoder_1_out0, bank_clock);
  and and_2 (and_2_out, decoder_1_out1, bank_clock);
  and and_3 (and_3_out, decoder_1_out2, bank_clock);
  and and_4 (and_4_out, decoder_1_out3, bank_clock);
  and and_5 (and_5_out, decoder_1_out4, bank_clock);
  and and_6 (and_6_out, decoder_1_out5, bank_clock);
  and and_7 (and_7_out, decoder_1_out6, bank_clock);
  Multiplexer #(.width(9)) multiplexer_1 (
    .in0(Register_0), .in1(Writing_), .out(multiplexer_1_out), .sel(Write_Enable));  // open: en
  Multiplexer #(.width(9)) multiplexer_2 (
    .in0(Register_1), .in1(Writing_), .out(multiplexer_2_out), .sel(Write_Enable));  // open: en
  Multiplexer #(.width(9)) multiplexer_3 (
    .in0(Register_2), .in1(Writing_), .out(multiplexer_3_out), .sel(Write_Enable));  // open: en
  Multiplexer #(.width(9)) multiplexer_4 (
    .in0(Register_3), .in1(Writing_), .out(multiplexer_4_out), .sel(Write_Enable));  // open: en
  Multiplexer #(.width(9)) multiplexer_5 (
    .in0(Register_4), .in1(Writing_), .out(multiplexer_5_out), .sel(Write_Enable));  // open: en
  Multiplexer #(.width(9)) multiplexer_6 (
    .in0(Register_5), .in1(Writing_), .out(multiplexer_6_out), .sel(Write_Enable));  // open: en
  Multiplexer #(.width(9)) multiplexer_7 (
    .in0(Register_6), .in1(Writing_), .out(multiplexer_7_out), .sel(Write_Enable));  // open: en
  D_Flip_Flop d_ff_1 (.clk(and_1_out), .D(multiplexer_1_out[8]), .Q(Register_0[8]));  // open: Qn, preset, en, reset
  D_Flip_Flop d_ff_2 (.clk(and_2_out), .D(multiplexer_2_out[8]), .Q(Register_1[8]));  // open: Qn, preset, en, reset
  D_Flip_Flop d_ff_3 (.clk(and_3_out), .D(multiplexer_3_out[8]), .Q(Register_2[8]));  // open: Qn, preset, en, reset
  D_Flip_Flop d_ff_4 (.clk(and_4_out), .D(multiplexer_4_out[8]), .Q(Register_3[8]));  // open: Qn, preset, en, reset
  D_Flip_Flop d_ff_5 (.clk(and_5_out), .D(multiplexer_5_out[8]), .Q(Register_4[8]));  // open: Qn, preset, en, reset
  D_Flip_Flop d_ff_6 (.clk(and_6_out), .D(multiplexer_6_out[8]), .Q(Register_5[8]));  // open: Qn, preset, en, reset
  D_Flip_Flop d_ff_7 (.clk(and_7_out), .D(multiplexer_7_out[8]), .Q(Register_6[8]));  // open: Qn, preset, en, reset
  D_Flip_Flop d_ff_8 (.clk(and_1_out), .D(multiplexer_1_out[7]), .Q(Register_0[7]));  // open: Qn, preset, en, reset
  D_Flip_Flop d_ff_9 (.clk(and_2_out), .D(multiplexer_2_out[7]), .Q(Register_1[7]));  // open: Qn, preset, en, reset
  D_Flip_Flop d_ff_10 (.clk(and_3_out), .D(multiplexer_3_out[7]), .Q(Register_2[7]));  // open: Qn, preset, en, reset
  D_Flip_Flop d_ff_11 (.clk(and_4_out), .D(multiplexer_4_out[7]), .Q(Register_3[7]));  // open: Qn, preset, en, reset
  D_Flip_Flop d_ff_12 (.clk(and_5_out), .D(multiplexer_5_out[7]), .Q(Register_4[7]));  // open: Qn, preset, en, reset
  D_Flip_Flop d_ff_13 (.clk(and_6_out), .D(multiplexer_6_out[7]), .Q(Register_5[7]));  // open: Qn, preset, en, reset
  D_Flip_Flop d_ff_14 (.clk(and_7_out), .D(multiplexer_7_out[7]), .Q(Register_6[7]));  // open: Qn, preset, en, reset
  D_Flip_Flop d_ff_15 (.clk(and_1_out), .D(multiplexer_1_out[6]), .Q(Register_0[6]));  // open: Qn, preset, en, reset
  D_Flip_Flop d_ff_16 (.clk(and_2_out), .D(multiplexer_2_out[6]), .Q(Register_1[6]));  // open: Qn, preset, en, reset
  D_Flip_Flop d_ff_17 (.clk(and_3_out), .D(multiplexer_3_out[6]), .Q(Register_2[6]));  // open: Qn, preset, en, reset
  D_Flip_Flop d_ff_18 (.clk(and_4_out), .D(multiplexer_4_out[6]), .Q(Register_3[6]));  // open: Qn, preset, en, reset
  D_Flip_Flop d_ff_19 (.clk(and_5_out), .D(multiplexer_5_out[6]), .Q(Register_4[6]));  // open: Qn, preset, en, reset
  D_Flip_Flop d_ff_20 (.clk(and_6_out), .D(multiplexer_6_out[6]), .Q(Register_5[6]));  // open: Qn, preset, en, reset
  D_Flip_Flop d_ff_21 (.clk(and_7_out), .D(multiplexer_7_out[6]), .Q(Register_6[6]));  // open: Qn, preset, en, reset
  D_Flip_Flop d_ff_22 (.clk(and_1_out), .D(multiplexer_1_out[5]), .Q(Register_0[5]));  // open: Qn, preset, en, reset
  D_Flip_Flop d_ff_23 (.clk(and_2_out), .D(multiplexer_2_out[5]), .Q(Register_1[5]));  // open: Qn, preset, en, reset
  D_Flip_Flop d_ff_24 (.clk(and_3_out), .D(multiplexer_3_out[5]), .Q(Register_2[5]));  // open: Qn, preset, en, reset
  D_Flip_Flop d_ff_25 (.clk(and_4_out), .D(multiplexer_4_out[5]), .Q(Register_3[5]));  // open: Qn, preset, en, reset
  D_Flip_Flop d_ff_26 (.clk(and_5_out), .D(multiplexer_5_out[5]), .Q(Register_4[5]));  // open: Qn, preset, en, reset
  D_Flip_Flop d_ff_27 (.clk(and_6_out), .D(multiplexer_6_out[5]), .Q(Register_5[5]));  // open: Qn, preset, en, reset
  D_Flip_Flop d_ff_28 (.clk(and_7_out), .D(multiplexer_7_out[5]), .Q(Register_6[5]));  // open: Qn, preset, en, reset
  D_Flip_Flop d_ff_29 (.clk(and_1_out), .D(multiplexer_1_out[4]), .Q(Register_0[4]));  // open: Qn, preset, en, reset
  D_Flip_Flop d_ff_30 (.clk(and_2_out), .D(multiplexer_2_out[4]), .Q(Register_1[4]));  // open: Qn, preset, en, reset
  D_Flip_Flop d_ff_31 (.clk(and_3_out), .D(multiplexer_3_out[4]), .Q(Register_2[4]));  // open: Qn, preset, en, reset
  D_Flip_Flop d_ff_32 (.clk(and_4_out), .D(multiplexer_4_out[4]), .Q(Register_3[4]));  // open: Qn, preset, en, reset
  D_Flip_Flop d_ff_33 (.clk(and_5_out), .D(multiplexer_5_out[4]), .Q(Register_4[4]));  // open: Qn, preset, en, reset
  D_Flip_Flop d_ff_34 (.clk(and_6_out), .D(multiplexer_6_out[4]), .Q(Register_5[4]));  // open: Qn, preset, en, reset
  D_Flip_Flop d_ff_35 (.clk(and_7_out), .D(multiplexer_7_out[4]), .Q(Register_6[4]));  // open: Qn, preset, en, reset
  D_Flip_Flop d_ff_36 (.clk(and_1_out), .D(multiplexer_1_out[3]), .Q(Register_0[3]));  // open: Qn, preset, en, reset
  D_Flip_Flop d_ff_37 (.clk(and_2_out), .D(multiplexer_2_out[3]), .Q(Register_1[3]));  // open: Qn, preset, en, reset
  D_Flip_Flop d_ff_38 (.clk(and_3_out), .D(multiplexer_3_out[3]), .Q(Register_2[3]));  // open: Qn, preset, en, reset
  D_Flip_Flop d_ff_39 (.clk(and_4_out), .D(multiplexer_4_out[3]), .Q(Register_3[3]));  // open: Qn, preset, en, reset
  D_Flip_Flop d_ff_40 (.clk(and_5_out), .D(multiplexer_5_out[3]), .Q(Register_4[3]));  // open: Qn, preset, en, reset
  D_Flip_Flop d_ff_41 (.clk(and_6_out), .D(multiplexer_6_out[3]), .Q(Register_5[3]));  // open: Qn, preset, en, reset
  D_Flip_Flop d_ff_42 (.clk(and_7_out), .D(multiplexer_7_out[3]), .Q(Register_6[3]));  // open: Qn, preset, en, reset
  D_Flip_Flop d_ff_43 (.clk(and_1_out), .D(multiplexer_1_out[1]), .Q(Register_0[1]));  // open: Qn, preset, en, reset
  D_Flip_Flop d_ff_44 (.clk(and_1_out), .D(multiplexer_1_out[2]), .Q(Register_0[2]));  // open: Qn, preset, en, reset
  D_Flip_Flop d_ff_45 (.clk(and_2_out), .D(multiplexer_2_out[2]), .Q(Register_1[2]));  // open: Qn, preset, en, reset
  D_Flip_Flop d_ff_46 (.clk(and_2_out), .D(multiplexer_2_out[1]), .Q(Register_1[1]));  // open: Qn, preset, en, reset
  D_Flip_Flop d_ff_47 (.clk(and_3_out), .D(multiplexer_3_out[1]), .Q(Register_2[1]));  // open: Qn, preset, en, reset
  D_Flip_Flop d_ff_48 (.clk(and_3_out), .D(multiplexer_3_out[2]), .Q(Register_2[2]));  // open: Qn, preset, en, reset
  D_Flip_Flop d_ff_49 (.clk(and_4_out), .D(multiplexer_4_out[2]), .Q(Register_3[2]));  // open: Qn, preset, en, reset
  D_Flip_Flop d_ff_50 (.clk(and_4_out), .D(multiplexer_4_out[1]), .Q(Register_3[1]));  // open: Qn, preset, en, reset
  D_Flip_Flop d_ff_51 (.clk(and_5_out), .D(multiplexer_5_out[1]), .Q(Register_4[1]));  // open: Qn, preset, en, reset
  D_Flip_Flop d_ff_52 (.clk(and_5_out), .D(multiplexer_5_out[2]), .Q(Register_4[2]));  // open: Qn, preset, en, reset
  D_Flip_Flop d_ff_53 (.clk(and_6_out), .D(multiplexer_6_out[1]), .Q(Register_5[1]));  // open: Qn, preset, en, reset
  D_Flip_Flop d_ff_54 (.clk(and_6_out), .D(multiplexer_6_out[2]), .Q(Register_5[2]));  // open: Qn, preset, en, reset
  D_Flip_Flop d_ff_55 (.clk(and_7_out), .D(multiplexer_7_out[1]), .Q(Register_6[1]));  // open: Qn, preset, en, reset
  D_Flip_Flop d_ff_56 (.clk(and_7_out), .D(multiplexer_7_out[2]), .Q(Register_6[2]));  // open: Qn, preset, en, reset
  D_Flip_Flop d_ff_57 (.clk(and_1_out), .D(multiplexer_1_out[0]), .Q(Register_0[0]));  // open: Qn, preset, en, reset
  D_Flip_Flop d_ff_58 (.clk(and_2_out), .D(multiplexer_2_out[0]), .Q(Register_1[0]));  // open: Qn, preset, en, reset
  D_Flip_Flop d_ff_59 (.clk(and_3_out), .D(multiplexer_3_out[0]), .Q(Register_2[0]));  // open: Qn, preset, en, reset
  D_Flip_Flop d_ff_60 (.clk(and_4_out), .D(multiplexer_4_out[0]), .Q(Register_3[0]));  // open: Qn, preset, en, reset
  D_Flip_Flop d_ff_61 (.clk(and_5_out), .D(multiplexer_5_out[0]), .Q(Register_4[0]));  // open: Qn, preset, en, reset
  D_Flip_Flop d_ff_62 (.clk(and_6_out), .D(multiplexer_6_out[0]), .Q(Register_5[0]));  // open: Qn, preset, en, reset
  D_Flip_Flop d_ff_63 (.clk(and_7_out), .D(multiplexer_7_out[0]), .Q(Register_6[0]));  // open: Qn, preset, en, reset
endmodule

module Counter_RAM (
  input  counter_clock,
  input  HALT,
  output [21:0] instruction
);

  wire and_1_out, and_2_out, and_3_out, multiplexer_1_out, not_1_out;
  wire [4:0] t_ff_1_q;

  not not_1 (not_1_out, 1'b1);
  Multiplexer multiplexer_1 (.in0(counter_clock), .in1(not_1_out), .out(multiplexer_1_out), .sel(HALT));  // open: en
  T_Flip_Flop t_ff_1 (.clk(multiplexer_1_out), .T(1'b1), .Q(t_ff_1_q[0]));  // open: Qn, preset, reset, en
  T_Flip_Flop t_ff_2 (.clk(multiplexer_1_out), .T(t_ff_1_q[0]), .Q(t_ff_1_q[1]));  // open: Qn, preset, reset, en
  and and_1 (and_1_out, t_ff_1_q[1], t_ff_1_q[0]);
  T_Flip_Flop t_ff_3 (.clk(multiplexer_1_out), .T(and_1_out), .Q(t_ff_1_q[2]));  // open: Qn, preset, reset, en
  and and_2 (and_2_out, t_ff_1_q[2], and_1_out);
  T_Flip_Flop t_ff_4 (.clk(multiplexer_1_out), .T(and_2_out), .Q(t_ff_1_q[3]));  // open: Qn, preset, reset, en
  and and_3 (and_3_out, t_ff_1_q[3], and_2_out);
  T_Flip_Flop t_ff_5 (.clk(multiplexer_1_out), .T(and_3_out), .Q(t_ff_1_q[4]));  // open: Qn, preset, reset, en
  RAM #(.addrWidth(5), .dataWidth(22), .bus("separate")) ram_1 (
    .addr(t_ff_1_q), .data(instruction), .str(1'b0), .clk(multiplexer_1_out), .ld(1'b1));  // open: din, sel, clr
endmodule

module ALU (
  input  [8:0] A_Input,
  input  [8:0] B_Input,
  input  [3:0] Operation,
  output [8:0] Alu_output
);

  wire [8:0] ADD_2_and_output, ADD_and_output, AND_and_output, NOT_2_not_output, NOT_not_output, OR_or_output;

  AND AND (.A_Input(B_Input), .B_Input(A_Input), .And_output(AND_and_output));
  OR OR (.A_Input(B_Input), .B_Input(A_Input), .OR_output(OR_or_output));
  NOT NOT (.A_Input(A_Input), .NOT_output(NOT_not_output));
  ADD ADD (.CIN(1'b0), .A_Input(A_Input), .B_Input(B_Input), .AND_output(ADD_and_output));
  NOT NOT_2 (.A_Input(B_Input), .NOT_output(NOT_2_not_output));
  ADD ADD_2 (.CIN(1'b1), .A_Input(A_Input), .B_Input(NOT_2_not_output), .AND_output(ADD_2_and_output));
  Multiplexer #(.select(4), .width(9)) multiplexer_1 (
    .in0(AND_and_output), .in1(OR_or_output), .in2(NOT_not_output), .in3(ADD_and_output), .in4(A_Input),
    .in5({A_Input[7:0], 1'b0}), .in6({1'b0, A_Input[8:1]}), .in7(ADD_2_and_output), .in8(ADD_and_output),
    .in9(ADD_2_and_output), .in10(B_Input), .in11(A_Input), .out(Alu_output), .sel(Operation));  // open: in12, in13, in14, in15, en
endmodule

module AND (
  input  [8:0] A_Input,
  input  [8:0] B_Input,
  output [8:0] And_output
);

  and and_1 (And_output[8], A_Input[8], B_Input[8]);
  and and_2 (And_output[7], A_Input[7], B_Input[7]);
  and and_3 (And_output[6], A_Input[6], B_Input[6]);
  and and_4 (And_output[5], A_Input[5], B_Input[5]);
  and and_5 (And_output[4], A_Input[4], B_Input[4]);
  and and_6 (And_output[3], A_Input[3], B_Input[3]);
  and and_7 (And_output[2], A_Input[2], B_Input[2]);
  and and_8 (And_output[0], A_Input[0], B_Input[0]);
  and and_9 (And_output[1], A_Input[1], B_Input[1]);
endmodule

module OR (
  input  [8:0] A_Input,
  input  [8:0] B_Input,
  output [8:0] OR_output
);

  or or_1 (OR_output[8], A_Input[8], B_Input[8]);
  or or_2 (OR_output[7], A_Input[7], B_Input[7]);
  or or_3 (OR_output[6], A_Input[6], B_Input[6]);
  or or_4 (OR_output[5], A_Input[5], B_Input[5]);
  or or_5 (OR_output[4], A_Input[4], B_Input[4]);
  or or_6 (OR_output[3], A_Input[3], B_Input[3]);
  or or_7 (OR_output[2], A_Input[2], B_Input[2]);
  or or_8 (OR_output[1], A_Input[1], B_Input[1]);
  or or_9 (OR_output[0], A_Input[0], B_Input[0]);
endmodule

module NOT (
  input  [8:0] A_Input,
  output [8:0] NOT_output
);

  not not_1 (NOT_output[6], A_Input[6]);
  not not_2 (NOT_output[8], A_Input[8]);
  not not_3 (NOT_output[7], A_Input[7]);
  not not_4 (NOT_output[4], A_Input[4]);
  not not_5 (NOT_output[5], A_Input[5]);
  not not_6 (NOT_output[3], A_Input[3]);
  not not_7 (NOT_output[2], A_Input[2]);
  not not_8 (NOT_output[1], A_Input[1]);
  not not_9 (NOT_output[0], A_Input[0]);
endmodule

module ADD (
  input  [8:0] A_Input,
  input  [8:0] B_Input,
  input  CIN,
  output [8:0] AND_output
);

  wire _0_g, _0_p, _1_g, _1_p, _2_g, _2_p, _3_g, _3_p, _4_g, _4_p, _5_g, _5_p, _6_g, _6_p, _7_g, _7_p,
       and_1_out, and_2_out, and_3_out, and_4_out, and_5_out, and_6_out, and_7_out, and_8_out, and_9_out,
       and_10_out, and_11_out, and_12_out, and_13_out, and_14_out, and_15_out, and_16_out, and_17_out,
       and_18_out, and_19_out, and_20_out, and_21_out, and_22_out, and_23_out, and_24_out, and_25_out,
       and_26_out, and_27_out, and_28_out, and_29_out, and_30_out, and_31_out, and_32_out, and_33_out,
       and_34_out, and_35_out, and_36_out, c1_out, c2_out, c3_out, c4_out, c5_2_out, c5_out, c6_out, c7_out;

  and and_1 (and_1_out, CIN, _0_p);
  or c1 (c1_out, and_1_out, _0_g);
  ADD_TOP _0 (.A(A_Input[0]), .B(B_Input[0]), .C(CIN), .G(_0_g), .P(_0_p), .S(AND_output[0]));
  and and_2 (and_2_out, CIN, _0_p, _1_p);
  ADD_TOP _1 (.A(A_Input[1]), .B(B_Input[1]), .C(c1_out), .G(_1_g), .P(_1_p), .S(AND_output[1]));
  and and_3 (and_3_out, _0_g, _1_p);
  or c2 (c2_out, and_2_out, and_3_out, _1_g);
  ADD_TOP _2 (.A(A_Input[2]), .B(B_Input[2]), .C(c2_out), .G(_2_g), .P(_2_p), .S(AND_output[2]));
  and and_4 (and_4_out, CIN, _0_p, _1_p, _2_p);
  and and_5 (and_5_out, _0_g, _2_p, _1_p);
  or c3 (c3_out, and_4_out, and_5_out, and_6_out, _2_g);
  and and_6 (and_6_out, _1_g, _2_p);
  ADD_TOP _3 (.A(A_Input[3]), .B(B_Input[3]), .C(c3_out), .G(_3_g), .P(_3_p), .S(AND_output[3]));
  and and_7 (and_7_out, CIN, _0_p, _1_p, _2_p, _3_p);
  and and_8 (and_8_out, _0_g, _3_p, _1_p, _2_p);
  and and_9 (and_9_out, _1_g, _2_p, _3_p);
  or c4 (c4_out, and_7_out, and_8_out, and_9_out, and_10_out, _3_g);
  and and_10 (and_10_out, _2_g, _3_p);
  and and_11 (and_11_out, CIN, _0_p, _1_p, _2_p, _3_p, _4_p);
  ADD_TOP _4 (.A(A_Input[4]), .B(B_Input[4]), .C(c4_out), .G(_4_g), .P(_4_p), .S(AND_output[4]));
  and and_12 (and_12_out, _0_g, _1_p, _2_p, _3_p, _4_p);
  or c5 (c5_out, and_11_out, and_12_out, and_13_out, and_14_out, and_15_out, _4_g);
  and and_13 (and_13_out, _1_g, _2_p, _3_p, _4_p);
  and and_14 (and_14_out, _2_g, _3_p, _4_p);
  and and_15 (and_15_out, _3_g, _4_p);
  and and_16 (and_16_out, CIN, _0_p, _1_p, _2_p, _3_p, _4_p, _5_p);
  ADD_TOP _5 (.A(A_Input[5]), .B(B_Input[5]), .C(c5_out), .G(_5_g), .P(_5_p), .S(AND_output[5]));
  and and_17 (and_17_out, _0_g, _1_p, _2_p, _3_p, _4_p, _5_p);
  and and_18 (and_18_out, _3_p, _4_p, _5_p, _2_g);
  and and_19 (and_19_out, _1_g, _2_p, _3_p, _4_p, _5_p);
  or c5_2 (c5_2_out, and_16_out, and_17_out, and_19_out, and_18_out, and_20_out, and_21_out, _5_g);
  and and_20 (and_20_out, _3_g, _4_p, _5_p);
  and and_21 (and_21_out, _4_g, _5_p);
  and and_22 (and_22_out, CIN, _0_p, _1_p, _2_p, _3_p, _4_p, _5_p, _6_p);
  ADD_TOP _6 (.A(A_Input[6]), .B(B_Input[6]), .C(c5_2_out), .G(_6_g), .P(_6_p), .S(AND_output[6]));
  and and_23 (and_23_out, _0_g, _1_p, _2_p, _3_p, _4_p, _5_p, _6_p);
  and and_24 (and_24_out, _1_g, _2_p, _3_p, _4_p, _5_p, _6_p);
  or c6 (c6_out, and_22_out, and_23_out, and_24_out, and_26_out, and_25_out, and_27_out, and_28_out, _6_g);
  and and_25 (and_25_out, _3_g, _4_p, _5_p, _6_p);
  and and_26 (and_26_out, _2_g, _3_p, _4_p, _5_p, _6_p);
  and and_27 (and_27_out, _4_g, _5_p, _6_p);
  and and_28 (and_28_out, _5_g, _6_p);
  and and_29 (and_29_out, CIN, _0_p, _1_p, _2_p, _3_p, _4_p, _5_p, _6_p, _7_p);
  ADD_TOP _7 (.A(A_Input[7]), .B(B_Input[7]), .C(c6_out), .G(_7_g), .P(_7_p), .S(AND_output[7]));
  and and_30 (and_30_out, _0_g, _1_p, _2_p, _3_p, _4_p, _5_p, _6_p, _7_p);
  and and_31 (and_31_out, _1_g, _2_p, _3_p, _4_p, _5_p, _6_p, _7_p);
  and and_32 (and_32_out, _2_g, _3_p, _4_p, _5_p, _6_p, _7_p);
  or c7 (c7_out, and_29_out, and_30_out, and_31_out, and_32_out, and_34_out, and_33_out, and_35_out, and_36_out, _7_g);
  and and_33 (and_33_out, _4_g, _5_p, _6_p, _7_p);
  and and_34 (and_34_out, _3_g, _4_p, _5_p, _6_p, _7_p);
  and and_35 (and_35_out, _5_g, _6_p, _7_p);
  and and_36 (and_36_out, _6_g, _7_p);
  ADD_TOP _8 (.A(A_Input[8]), .B(B_Input[8]), .C(c7_out), .S(AND_output[8]));  // open: G, P
endmodule

module ADD_TOP (
  input  A,
  input  B,
  input  C,
  output G,
  output P,
  output S
);

  and u_g (G, A, B);
  or u_p (P, B, A);
  xor u_s (S, B, A, C);
endmodule
